// Logisim project atto-8.circ as structural Verilog: 1 circuit, main circuit main
module main (
);

  wire and_2_out, and_3_out, and_4_out, and_5_out, and_6_out, and_7_out, and_8_out, button_9_out, CIN, CLK,
       CLR_SC, counter_1_carry, counter_2_carry, COUT, COUT_CF, DATA_AL, DATA_IL, DATA_IP, DATA_MEM, DATA_SP,
       DATA_XL, DATA_YL, DATA_ZL, demultiplexer_1_out0, demultiplexer_1_out1, demultiplexer_1_out2,
       demultiplexer_1_out3, demultiplexer_1_out4, demultiplexer_1_out5, demultiplexer_1_out6,
       demultiplexer_1_out7, demultiplexer_1_out8, demultiplexer_1_out9, demultiplexer_1_out10,
       demultiplexer_1_out11, demultiplexer_1_out12, demultiplexer_1_out13, demultiplexer_1_out14,
       demultiplexer_1_out15, demultiplexer_1_out16, demultiplexer_1_out17, demultiplexer_1_out18,
       demultiplexer_1_out19, demultiplexer_1_out20, demultiplexer_1_out21, demultiplexer_1_out22,
       demultiplexer_1_out23, demultiplexer_1_out24, demultiplexer_1_out25, demultiplexer_1_out26,
       demultiplexer_1_out27, demultiplexer_1_out28, demultiplexer_1_out29, demultiplexer_1_out30,
       demultiplexer_1_out31, INHIBIT, IP_DATA, keyboard_1_avail, MEM_DATA, multiplexer_1_out, NAND_DATA,
       not_1_out, not_2_out, not_3_out, not_4_out, not_5_out, not_7_out, NUL, OFST_AND_CF, OFST_DATA,
       ONES_DATA, or_1_out, or_2_out, or_3_out, or_4_out, RST, s_r_ff_1_q, s_r_ff_1_qn, SIZE_AND_CIN,
       SIZE_DATA, SP_DATA, SUM_DATA, undriven, ZERO, ZERO_CF;
  wire [3:0] demultiplexer_2_out0, register_40_q;
  wire [4:0] counter_1_q;
  wire [5:5] register_39_q;
  wire [6:0] keyboard_1_data;
  wire [7:0] adder_1_out, ADDR, button_1_out, DATA, MCADDR, MCDATA, multiplexer_2_out, nand_1_out, or_5_out,
       register_1_q, register_2_q, register_3_q, register_4_q, register_5_q, register_7_q, register_8_q,
       register_9_q, register_10_q, register_11_q, register_12_q, register_13_q, register_14_q,
       register_15_q, register_16_q, register_17_q, register_18_q, register_19_q, register_20_q,
       register_21_q, register_22_q, register_23_q, register_24_q, register_25_q, register_26_q,
       register_27_q, register_28_q, register_29_q, register_30_q, register_31_q, register_32_q,
       register_33_q, register_34_q, register_35_q, register_36_q, register_37_q, register_38_q, ROM0_data;
  wire [7:4] register_40_q_2;
  wire [7:7] not_6_out;
  wire [8:0] counter_2_q;

  S_R_Flip_Flop s_r_ff_1 (
    .S(NUL), .R(1'b0), .clk(not_1_out), .Q(s_r_ff_1_q), .reset(RST), .Qn(s_r_ff_1_qn), .preset(1'b0));
  not not_1 (not_1_out, MEM_DATA);
  Register register_1 (.D(DATA), .en(DATA_XL), .clk(CLK), .Q(register_1_q), .clr(RST));
  LedBar ledbar_1 (
    .led0(register_1_q[7]), .led1(register_1_q[6]), .led2(register_1_q[5]), .led3(register_1_q[4]),
    .led4(register_1_q[3]), .led5(register_1_q[2]), .led6(register_1_q[1]), .led7(register_1_q[0]));
  Register register_2 (.D(DATA), .en(DATA_YL), .clk(CLK), .Q(register_2_q), .clr(RST));
  LedBar ledbar_2 (
    .led0(register_2_q[7]), .led1(register_2_q[6]), .led2(register_2_q[5]), .led3(register_2_q[4]),
    .led4(register_2_q[3]), .led5(register_2_q[2]), .led6(register_2_q[1]), .led7(register_2_q[0]));
  Register register_3 (.D(DATA), .en(DATA_ZL), .clk(CLK), .Q(register_3_q), .clr(RST));
  LedBar ledbar_3 (
    .led0(register_3_q[7]), .led1(register_3_q[6]), .led2(register_3_q[5]), .led3(register_3_q[4]),
    .led4(register_3_q[3]), .led5(register_3_q[2]), .led6(register_3_q[1]), .led7(register_3_q[0]));
  Register register_4 (.D(DATA), .en(DATA_IP), .clk(CLK), .Q(register_4_q), .clr(RST));
  LedBar ledbar_4 (
    .led0(register_4_q[7]), .led1(register_4_q[6]), .led2(register_4_q[5]), .led3(register_4_q[4]),
    .led4(register_4_q[3]), .led5(register_4_q[2]), .led6(register_4_q[1]), .led7(register_4_q[0]));
  Register register_5 (.D(DATA), .en(DATA_SP), .clk(CLK), .Q(register_5_q), .clr(RST));
  LedBar ledbar_5 (
    .led0(register_5_q[7]), .led1(register_5_q[6]), .led2(register_5_q[5]), .led3(register_5_q[4]),
    .led4(register_5_q[3]), .led5(register_5_q[2]), .led6(register_5_q[1]), .led7(register_5_q[0]));
  Register register_6 (.D(DATA), .en(DATA_AL), .clk(CLK), .Q(ADDR), .clr(RST));
  LedBar ledbar_6 (
    .led0(ADDR[7]), .led1(ADDR[6]), .led2(ADDR[5]), .led3(ADDR[4]), .led4(ADDR[3]), .led5(ADDR[2]),
    .led6(ADDR[1]), .led7(ADDR[0]));
  nor nor_1 (NUL, MCADDR[0], MCADDR[1], MCADDR[2], MCADDR[3], MCADDR[4], MCADDR[5], MCADDR[6], MCADDR[7]);
  and and_1 (INHIBIT, NUL, s_r_ff_1_q);
  // NoConnect on s_r_ff_1_qn
  not not_2 (not_2_out, INHIBIT);
  RAM #(.asyncread("true"), .databus("bidir")) MEM (
    .addr(MCADDR), .we(or_1_out), .oe(and_2_out), .clk(CLK), .data(MCDATA));
  or or_1 (or_1_out, DATA_MEM, RST);
  and and_2 (and_2_out, MEM_DATA, not_2_out);
  Adder adder_1 (.a(register_1_q), .b(register_2_q), .out(adder_1_out), .cin(CIN), .cout(COUT));
  assign nand_1_out = ~(register_2_q & register_3_q);  // NAND_Gate nand_1, 8 bits wide
  nor nor_2 (ZERO, nand_1_out[0], nand_1_out[1], nand_1_out[2], nand_1_out[3], nand_1_out[4], nand_1_out[5], nand_1_out[6], nand_1_out[7]);
  assign DATA = IP_DATA ? register_4_q : 8'bz;  // Controlled_Buffer controlled_buffer_1
  assign DATA = SP_DATA ? register_5_q : 8'bz;  // Controlled_Buffer controlled_buffer_2
  Demultiplexer #(.select(5)) demultiplexer_1 (
    .out0(demultiplexer_1_out0), .out1(demultiplexer_1_out1), .out2(demultiplexer_1_out2),
    .out3(demultiplexer_1_out3), .out4(demultiplexer_1_out4), .out5(demultiplexer_1_out5),
    .out6(demultiplexer_1_out6), .out7(demultiplexer_1_out7), .out8(demultiplexer_1_out8),
    .out9(demultiplexer_1_out9), .out10(demultiplexer_1_out10), .out11(demultiplexer_1_out11),
    .out12(demultiplexer_1_out12), .out13(demultiplexer_1_out13), .out14(demultiplexer_1_out14),
    .out15(demultiplexer_1_out15), .out16(demultiplexer_1_out16), .out17(demultiplexer_1_out17),
    .out18(demultiplexer_1_out18), .out19(demultiplexer_1_out19), .out20(demultiplexer_1_out20),
    .out21(demultiplexer_1_out21), .out22(demultiplexer_1_out22), .out23(demultiplexer_1_out23),
    .out24(demultiplexer_1_out24), .out25(demultiplexer_1_out25), .out26(demultiplexer_1_out26),
    .out27(demultiplexer_1_out27), .out28(demultiplexer_1_out28), .out29(demultiplexer_1_out29),
    .out30(demultiplexer_1_out30), .out31(demultiplexer_1_out31), .in(1'b1), .sel(MCADDR[4:0]));
  and and_3 (and_3_out, MCADDR[5], MCADDR[6], MCADDR[7]);
  or or_2 (or_2_out, DATA_MEM, RST);
  LedBar ledbar_7 (
    .led0(adder_1_out[7]), .led1(adder_1_out[6]), .led2(adder_1_out[5]), .led3(adder_1_out[4]),
    .led4(adder_1_out[3]), .led5(adder_1_out[2]), .led6(adder_1_out[1]), .led7(adder_1_out[0]));
  LedBar ledbar_8 (
    .led0(nand_1_out[7]), .led1(nand_1_out[6]), .led2(nand_1_out[5]), .led3(nand_1_out[4]),
    .led4(nand_1_out[3]), .led5(nand_1_out[2]), .led6(nand_1_out[1]), .led7(nand_1_out[0]));
  LedBar ledbar_9 (
    .led0(1'b1), .led1(1'b1), .led2(1'b1), .led3(1'b1), .led4(1'b1), .led5(1'b1), .led6(1'b1), .led7(1'b1));
  not not_3 (not_3_out, RST);
  assign MCADDR = not_3_out ? ADDR : 8'bz;  // Controlled_Buffer controlled_buffer_3
  and and_4 (and_4_out, and_3_out, or_2_out, CLK);
  assign DATA = SUM_DATA ? adder_1_out : 8'bz;  // Controlled_Buffer controlled_buffer_4
  assign DATA = NAND_DATA ? nand_1_out : 8'bz;  // Controlled_Buffer controlled_buffer_5
  assign DATA = ONES_DATA ? {8{1'b1}} : 8'bz;  // Controlled_Buffer controlled_buffer_6
  and and_5 (and_5_out, not_3_out, DATA_MEM);
  assign MCDATA = and_5_out ? DATA : 8'bz;  // Controlled_Buffer controlled_buffer_7
  LedBar ledbar_10 (
    .led0(DATA[7]), .led1(DATA[6]), .led2(DATA[5]), .led3(DATA[4]), .led4(DATA[3]), .led5(DATA[2]),
    .led6(DATA[1]), .led7(DATA[0]));
  assign DATA = OFST_DATA ? {4'b0000, register_40_q} : 8'bz;  // Controlled_Buffer controlled_buffer_8
  assign DATA = SIZE_DATA ? {4'b0000, demultiplexer_2_out0} : 8'bz;  // Controlled_Buffer controlled_buffer_9
  assign DATA = and_6_out ? MCDATA : 8'bz;  // Controlled_Buffer controlled_buffer_10
  and and_6 (and_6_out, not_3_out, MEM_DATA);
  Register register_7 (.D(MCDATA), .en(demultiplexer_1_out1), .clk(and_4_out), .Q(register_7_q), .clr(undriven));
  Register register_8 (.D(MCDATA), .en(demultiplexer_1_out3), .clk(and_4_out), .Q(register_8_q), .clr(undriven));
  Register register_9 (.D(MCDATA), .en(demultiplexer_1_out5), .clk(and_4_out), .Q(register_9_q), .clr(undriven));
  Register register_10 (.D(MCDATA), .en(demultiplexer_1_out7), .clk(and_4_out), .Q(register_10_q), .clr(undriven));
  Register register_11 (.D(MCDATA), .en(demultiplexer_1_out9), .clk(and_4_out), .Q(register_11_q), .clr(undriven));
  Register register_12 (.D(MCDATA), .en(demultiplexer_1_out11), .clk(and_4_out), .Q(register_12_q), .clr(undriven));
  Register register_13 (.D(MCDATA), .en(demultiplexer_1_out13), .clk(and_4_out), .Q(register_13_q), .clr(undriven));
  Register register_14 (.D(MCDATA), .en(demultiplexer_1_out15), .clk(and_4_out), .Q(register_14_q), .clr(undriven));
  Register register_15 (.D(MCDATA), .en(demultiplexer_1_out14), .clk(and_4_out), .Q(register_15_q), .clr(undriven));
  Register register_16 (.D(MCDATA), .en(demultiplexer_1_out12), .clk(and_4_out), .Q(register_16_q), .clr(undriven));
  Register register_17 (.D(MCDATA), .en(demultiplexer_1_out10), .clk(and_4_out), .Q(register_17_q), .clr(undriven));
  Register register_18 (.D(MCDATA), .en(demultiplexer_1_out8), .clk(and_4_out), .Q(register_18_q), .clr(undriven));
  Register register_19 (.D(MCDATA), .en(demultiplexer_1_out6), .clk(and_4_out), .Q(register_19_q), .clr(undriven));
  Register register_20 (.D(MCDATA), .en(demultiplexer_1_out4), .clk(and_4_out), .Q(register_20_q), .clr(undriven));
  Register register_21 (.D(MCDATA), .en(demultiplexer_1_out2), .clk(and_4_out), .Q(register_21_q), .clr(undriven));
  Register register_22 (.D(MCDATA), .en(demultiplexer_1_out0), .clk(and_4_out), .Q(register_22_q), .clr(undriven));
  Register register_23 (.D(MCDATA), .en(demultiplexer_1_out30), .clk(and_4_out), .Q(register_23_q), .clr(undriven));
  Register register_24 (.D(MCDATA), .en(demultiplexer_1_out28), .clk(and_4_out), .Q(register_24_q), .clr(undriven));
  Register register_25 (.D(MCDATA), .en(demultiplexer_1_out26), .clk(and_4_out), .Q(register_25_q), .clr(undriven));
  Register register_26 (.D(MCDATA), .en(demultiplexer_1_out24), .clk(and_4_out), .Q(register_26_q), .clr(undriven));
  Register register_27 (.D(MCDATA), .en(demultiplexer_1_out22), .clk(and_4_out), .Q(register_27_q), .clr(undriven));
  Register register_28 (.D(MCDATA), .en(demultiplexer_1_out20), .clk(and_4_out), .Q(register_28_q), .clr(undriven));
  Register register_29 (.D(MCDATA), .en(demultiplexer_1_out18), .clk(and_4_out), .Q(register_29_q), .clr(undriven));
  Register register_30 (.D(MCDATA), .en(demultiplexer_1_out16), .clk(and_4_out), .Q(register_30_q), .clr(undriven));
  Register register_31 (.D(MCDATA), .en(demultiplexer_1_out17), .clk(and_4_out), .Q(register_31_q), .clr(undriven));
  Register register_32 (.D(MCDATA), .en(demultiplexer_1_out19), .clk(and_4_out), .Q(register_32_q), .clr(undriven));
  Register register_33 (.D(MCDATA), .en(demultiplexer_1_out21), .clk(and_4_out), .Q(register_33_q), .clr(undriven));
  Register register_34 (.D(MCDATA), .en(demultiplexer_1_out23), .clk(and_4_out), .Q(register_34_q), .clr(undriven));
  Register register_35 (.D(MCDATA), .en(demultiplexer_1_out25), .clk(and_4_out), .Q(register_35_q), .clr(undriven));
  Register register_36 (.D(MCDATA), .en(demultiplexer_1_out27), .clk(and_4_out), .Q(register_36_q), .clr(undriven));
  Register register_37 (.D(MCDATA), .en(demultiplexer_1_out29), .clk(and_4_out), .Q(register_37_q), .clr(undriven));
  Register register_38 (.D(MCDATA), .en(demultiplexer_1_out31), .clk(and_4_out), .Q(register_38_q), .clr(undriven));
  // NoConnect on MCDATA[7]
  TTY tty_1 (.data(MCDATA[6:0]), .clk(CLK), .we(and_7_out), .clr(RST));
  and and_7 (and_7_out, NUL, DATA_MEM);
  DotMatrix #(.inputtype("row"), .matrixcols(8), .matrixrows(8)) dotmatrix_1 (
    .row0(register_22_q), .row1(register_21_q), .row2(register_20_q), .row3(register_19_q),
    .row4(register_18_q), .row5(register_17_q), .row6(register_16_q), .row7(register_15_q));
  DotMatrix #(.inputtype("row"), .matrixcols(8), .matrixrows(8)) dotmatrix_2 (
    .row0(register_30_q), .row1(register_29_q), .row2(register_28_q), .row3(register_27_q),
    .row4(register_26_q), .row5(register_25_q), .row6(register_24_q), .row7(register_23_q));
  Counter #(.max('h1f), .width(5)) counter_1 (
    .clr(or_3_out), .load(1'b0), .up(1'b1), .count(not_4_out), .clk(not_5_out), .carry(counter_1_carry),
    .Q(counter_1_q));  // open: D
  or or_3 (or_3_out, RST, CLR_SC);
  not not_4 (not_4_out, RST);
  not not_5 (not_5_out, CLK);
  Multiplexer multiplexer_1 (.in0(COUT), .in1(ZERO), .out(multiplexer_1_out), .sel(ZERO_CF));
  Demultiplexer #(.select(2)) demultiplexer_2 (
    .out0(demultiplexer_2_out0[0]), .out1(demultiplexer_2_out0[1]), .out2(demultiplexer_2_out0[2]),
    .out3(demultiplexer_2_out0[3]), .in(1'b1), .sel(register_40_q[1:0]));
  Button button_1 (.out(button_1_out[0]));
  Button button_2 (.out(button_1_out[3]));
  Button button_3 (.out(button_1_out[1]));
  Keyboard #(.buflen(256)) keyboard_1 (
    .clk(CLK), .re(and_8_out), .clr(RST), .avail(keyboard_1_avail), .data(keyboard_1_data));
  // DotMatrix #(.inputtype("row"), .matrixcols(8), .matrixrows(8)) dotmatrix_3: pin names not known; wires that end beside it: register_7_q, register_8_q, register_9_q, register_10_q, register_11_q
  // DotMatrix #(.inputtype("row"), .matrixcols(8), .matrixrows(8)) dotmatrix_4: pin names not known; wires that end beside it: register_12_q, register_13_q, register_14_q, register_31_q, register_32_q, register_33_q, register_34_q, register_35_q, register_36_q, register_37_q, register_38_q
  LedBar #(.matrixcols(5)) ledbar_11 (
    .led0(counter_1_q[4]), .led1(counter_1_q[3]), .led2(counter_1_q[2]), .led3(counter_1_q[1]),
    .led4(counter_1_q[0]));
  Register #(.width(1)) register_39 (.D(multiplexer_1_out), .en(or_4_out), .clk(CLK), .Q(register_39_q[5]), .clr(RST));
  or or_4 (or_4_out, ZERO_CF, COUT_CF);
  Register register_40 (.D(DATA), .en(DATA_IL), .clk(CLK), .Q({register_40_q_2, register_40_q}), .clr(RST));
  LedBar ledbar_12 (
    .led0(register_40_q_2[7]), .led1(register_40_q_2[6]), .led2(register_40_q_2[5]),
    .led3(register_40_q_2[4]), .led4(register_40_q[3]), .led5(register_40_q[2]), .led6(register_40_q[1]),
    .led7(register_40_q[0]));
  Button button_4 (.out(button_1_out[4]));
  Button button_5 (.out(button_1_out[7]));
  Button button_6 (.out(button_1_out[2]));
  Button button_7 (.out(button_1_out[5]));
  and and_8 (and_8_out, MEM_DATA, INHIBIT);
  // NoConnect on counter_1_carry
  LedBar #(.matrixcols(1)) ledbar_13 (.led0(register_39_q[5]));
  not not_6 (not_6_out[7], register_40_q_2[7]);
  Clock #(.phaseOffset(1)) clock_1 (.out(CLK));
  Button button_8 (.out(button_1_out[6]));
  // NoConnect on or_5_out[7]
  assign or_5_out = {{4{not_6_out[7]}}, 4'b0000} | {register_40_q_2, register_40_q};  // OR_Gate or_5, 8 bits wide
  Button button_9 (.out(button_9_out));
  Multiplexer #(.width(8)) multiplexer_2 (
    .in0(button_1_out), .in1({1'b0, keyboard_1_data}), .out(multiplexer_2_out), .sel(keyboard_1_avail));
  ROM #(.addrWidth(13), .dataWidth(16)) MIC (
    .addr({or_5_out[6:0], register_39_q[5], counter_1_q}),
    .data({CLR_SC, DATA_IL, SIZE_AND_CIN, OFST_AND_CF, IP_DATA, DATA_IP, SP_DATA, DATA_SP, DATA_AL, MEM_DATA, DATA_MEM, DATA_XL, DATA_YL, DATA_ZL, SUM_DATA, NAND_DATA}));
  Counter #(.max('h1ff), .width(9)) counter_2 (
    .clr(button_9_out), .load(1'b0), .up(1'b1), .count(RST), .clk(not_7_out), .carry(counter_2_carry),
    .Q(counter_2_q));  // open: D
  not not_7 (not_7_out, CLK);
  assign MCDATA = and_8_out ? multiplexer_2_out : 8'bz;  // Controlled_Buffer controlled_buffer_11
  Demultiplexer #(.select(2)) demultiplexer_3 (
    .out0(OFST_DATA), .out1(COUT_CF), .out2(ZERO_CF), .in(OFST_AND_CF), .sel({NAND_DATA, SUM_DATA}));  // open: out3
  Demultiplexer demultiplexer_4 (.out0(SIZE_DATA), .out1(CIN), .in(SIZE_AND_CIN), .sel(SUM_DATA));
  LedBar #(.matrixcols(16)) ledbar_14 (
    .led0(NAND_DATA), .led1(SUM_DATA), .led2(DATA_ZL), .led3(DATA_YL), .led4(DATA_XL), .led5(DATA_MEM),
    .led6(MEM_DATA), .led7(DATA_AL), .led8(DATA_SP), .led9(SP_DATA), .led10(DATA_IP), .led11(IP_DATA),
    .led12(OFST_AND_CF), .led13(SIZE_AND_CIN), .led14(DATA_IL), .led15(CLR_SC));
  nor nor_3 (ONES_DATA, SIZE_DATA, OFST_DATA, IP_DATA, SP_DATA, SUM_DATA, NAND_DATA, MEM_DATA);
  // NoConnect on counter_2_carry
  assign MCADDR = RST ? counter_2_q[7:0] : 8'bz;  // Controlled_Buffer controlled_buffer_12
  ROM ROM0 (.addr(counter_2_q[7:0]), .data(ROM0_data));
  not not_8 (RST, counter_2_q[8]);
  assign MCDATA = RST ? ROM0_data : 8'bz;  // Controlled_Buffer controlled_buffer_13

  // Other names for the same wires on the sheet: WRT = DATA_MEM; READ = MEM_DATA; SET_CIN = CIN

  // Notes on the sheet:
  //   XL
  //   YL
  //   ZL
  //   IP
  //   SP
  //   AL
  //   SUM
  //   NAND
  //   ONES
  //   MEM
  //   ADDR
  //   DATA
  //   IL
  //   SC
  //   CF
  //   OFST
  //   SIZE
  //   . . . . . . . . . . . . . . . . . . . . . . . . . . . . . . . . . . . . . . . . . . . . . . . . . . . . . . . . . . . . . . . . . . . . . . . . . . . . . . . . . . . . . . . . . . . . . . . . . . . . . . . . . . . . . . . . . . . . . . . . . . . . . . . . . . . . . . . . . . . . . . . . . . . . . . . . . . . . . . . . . . . . . . . . 
  //   CLK
  //   MIC
  //   RST
  //   CTRL
  //   Atto-8 Microprocessor
  //   Atto-8 Microcomputer
endmodule
